# Fritzing sketch Railway_Crossing (saved by Fritzing 0.9.3b)
breadboards: 3

parts:
  Part1 = Arduino Uno (Rev3)
  hc-sr1 = hc-sr04
  hc-sr2 = hc-sr04
  J1 = Basic Servo
  LED1 = LED - 3mm [color="Red (633nm)" package="3 mm [THT]"]
  R1 = Resistor [tolerance=±5% resistance=220 package="0402 [SMD]"]

nets:
  N1: Part1.D9_PWM, J1.pulse
  N2: Part1.D13/SCK, LED1.anode
  GND: Part1.GND, hc-sr1.GND, hc-sr2.GND, J1.gnd, R1.Pin_1
  N3: Part1.D3_PWM, hc-sr2.Trig
  N4: Part1.D4, hc-sr2.Echo
  N5: Part1.D6_PWM, hc-sr1.Trig
  N6: Part1.D7, hc-sr1.Echo
  VCC: Part1.5V, hc-sr1.VCC, hc-sr2.VCC
  N7: LED1.cathode, R1.Pin_0
