# Fritzing sketch schematics (saved by Fritzing 0.9.3b)
breadboards: 1

parts:
  Part1 = Arduino Uno (Rev3)
  LED1 = LED - 3mm [color="Red (633nm)" package="3 mm [THT]"]
  U1 = TCRT5000 [package=THT]
  U2 = TCRT5000 [package=THT]
  U3 = TCRT5000 [package=THT]
  U4 = TCRT5000 [package=THT]
  R1 = Resistor [tolerance=±5% resistance=220 package=THT]
  R2 = Resistor [tolerance=±5% resistance=220 package=THT]
  R3 = Resistor [tolerance=±5% resistance=220 package=THT]
  R4 = Resistor [tolerance=±5% resistance=220 package=THT]
  R5 = Resistor [tolerance=±5% resistance=10k package=THT]
  R6 = Resistor [tolerance=±5% resistance=220 package=THT]
  R7 = Resistor [tolerance=±5% resistance=10k package=THT]
  R8 = Resistor [tolerance=±5% resistance=10k package=THT]
  R9 = Resistor [tolerance=±5% resistance=10k package=THT]
  J1 = Basic Servo

nets:
  N1: Part1.A0, U1.Pin_1, R1.Pin_1
  N2: Part1.A1, U3.Pin_1, R2.Pin_1
  N3: Part1.A3, U2.Pin_1, R3.Pin_1
  N4: Part1.A4/SDA, U4.Pin_1, R4.Pin_1
  N5: Part1.D9_PWM, J1.pulse
  N6: Part1.D13/SCK, LED1.anode
  5V: Part1.5V, U1.Pin_4, U2.Pin_4, U3.Pin_4, U4.Pin_4, R1.Pin_0, R2.Pin_0, R3.Pin_0, R4.Pin_0, J1.vcc
  GND: Part1.GND, U2.Pin_2, U4.Pin_2, R5.Pin_1, R7.Pin_1, J1.gnd
  N7: LED1.cathode, R6.Pin_0
  N8: U1.Pin_2, U3.Pin_2, R6.Pin_1, R8.Pin_1, R9.Pin_1
  N9: U1.Pin_3, R9.Pin_0
  N10: U2.Pin_3, R7.Pin_0
  N11: U3.Pin_3, R8.Pin_0
  N12: U4.Pin_3, R5.Pin_0

custom parts:
  TCRT5000: TCRT5000 optical reflective sensor
